# Fritzing sketch ES_Schaltplan (saved by Fritzing 1.0.8)

parts:
  MCU1 = Raspberry Pi Zero
  Bauteil1 = InvenSense MPU6050
  3_2_zoll_Touch_Screen1 = LCD TFT 2.8 Zoll
  U1 = SUP500F [package=sup500f]

nets:
  VCC: MCU1.pin_1, MCU1.pin_17, 3_2_zoll_Touch_Screen1.VCC, U1.VCC
  N1: MCU1.pin_2, MCU1.pin_4, Bauteil1.VCC
  N2: MCU1.pin_3, Bauteil1.SDA
  N3: MCU1.pin_5, Bauteil1.SCL
  GND: MCU1.pin_6, MCU1.pin_9, MCU1.pin_14, MCU1.pin_34, MCU1.pin_39, Bauteil1.GND, 3_2_zoll_Touch_Screen1.GND, U1.GND
  N4: MCU1.pin_8, U1.RX-I
  N5: MCU1.pin_10, U1.TX-O
  N6: MCU1.pin_12, 3_2_zoll_Touch_Screen1.BL
  N7: MCU1.pin_13, 3_2_zoll_Touch_Screen1.RST
  N8: MCU1.pin_19, 3_2_zoll_Touch_Screen1.DIN
  N9: MCU1.pin_21, 3_2_zoll_Touch_Screen1.CLK
  N10: MCU1.pin_22, 3_2_zoll_Touch_Screen1.DC
  N11: MCU1.pin_24, 3_2_zoll_Touch_Screen1.CS

custom parts:
  LCD TFT 2.8 Zoll: DollaTek tft touch screen lcd display
  SUP500F: SUP500F Venus GPS
